# Fritzing sketch microsensor (saved by Fritzing 0.6.5b)
breadboards: 2

parts:
  Arduino1 = Arduino
  MIC1 = Microphone
  C4 = Ceramic Capacitor [package=THT]
  U1 = LM 358 Dual Op-Amp [package="DIP8 [THT]"]
  D1 = Rectifier Diode [part_number=1N4001 package="300 mil [THT]"]
  R1 = Resistor [resistance=2.2 tolerance=±5% package=THT]
  R2 = Resistor [resistance=2.2 tolerance=±5% package=THT]
  C2 = Electrolytic Capacitor [package=THT]
  C1 = Electrolytic Capacitor [package=THT]
  C3 = Electrolytic Capacitor [package=THT]

nets:
  N1: Arduino1.GND, MIC1.pin1, C4.pin_0, U1.connector1, U1.connector3, R1.Pin_0, C2.-, C3.-
  N2: Arduino1.+5V, R2.Pin_1, C3.+
  N3: Arduino1.A0, D1.cathode, R1.Pin_1, C2.+
  N4: MIC1.pin2, C4.pin_1, R2.Pin_0
  N5: U1.connector0, C1.-
  N6: U1.connector4, D1.anode
  N7: U1.connector7, C1.+

notes:
  uF pF
