# Fritzing sketch amp (saved by Fritzing 0.8.5b)
circuit board: 4.94213cm x 2.85195cm
breadboards: 1

parts:
  U1 = LM386 [package=dip08]
  J1 = Screw terminal - 2 pins [package=THT]
  R1 = Resistor [tolerance=±5% resistance=10 package=THT]
  C1 = Electrolytic Capacitor [capacitance=0.1µF package="100 mil [THT, electrolytic]"]
  R3 = Resistor [tolerance=±5% resistance=10k package=THT]
  C3 = Electrolytic Capacitor [capacitance=10µF package="100 mil [THT, electrolytic]"]
  C2 = Electrolytic Capacitor [capacitance=0.25mF voltage=16V package="100 mil [THT, electrolytic]"]
  Entrada = Audio Jack (TRS) 3.5mm [package="4Ucon 08780 [THT]"]
  audifonos = Audio Jack (TRS) 3.5mm [package="4Ucon 08780 [THT]"]
  Volumen = Rotary Potentiometer (Large) [package=THT]

nets:
  N1: U1.GAIN, R3.Pin_0, C3.-
  GND: U1.-IN, U1.V-, J1.pin1, C1.-, Entrada.Sleeve, audifonos.Sleeve, Volumen.leg2
  N2: U1.+IN, Volumen.wiper
  N3: U1.OUT, R1.Pin_1, C2.+
  N4: U1.V+, J1.pin2
  N5: R1.Pin_0, C1.+
  N6: R3.Pin_1, C3.+
  N7: C2.-, audifonos.Ring, audifonos.Tip
  N8: Entrada.Tip, Volumen.leg1

notes:
  - +
  City
  Listeners
  lessnullvoid.cc
  (( - ))
